// Logisim project 8051.circ as structural Verilog: 16 circuits, main circuit main
module main (
  output [7:0] out_1,
  output [7:0] out_2,
  output [7:0] out_3,
  output [7:0] out_4,
  output [7:0] out_5,
  output [7:0] out_6,
  output [7:0] out_7,
  output [7:0] out_8,
  output [7:0] out_9,
  output [7:0] out_10,
  output [7:0] out_11,
  output [7:0] out_12,
  output [7:0] out_13,
  output [7:0] out_14
);

  wire alu_1_a_larger, alu_1_carry_out, alu_1_equal, alu_1_zero, and_1_out, clock_1_out, cu_1_acc_e,
       cu_1_acc_s, cu_1_flags_s, cu_1_iar_s, cu_1_ir_s, cu_1_mar_s, cu_1_pc_e, cu_1_pc_inc, cu_1_pc_s,
       cu_1_ram_e, cu_1_ram_s, cu_1_rom_e, cu_1_stop_ci, cu_1_temp_s, cu_1_tmp_reset, Flagi_al_out,
       Flagi_c_out, Flagi_eq_out, Flagi_z_out, generato_enable_set_1_enable, generato_enable_set_1_set, R0e,
       R0s, R1e, R1s, R2e, R2s, R3e, R3s, R4e, R4s, R5e, R5s, R6e, R6s, R7e, R7s, reset_out;
  wire [2:0] cu_1_op;
  wire [7:0] ACC_o, alu_1_o, ir_1_o, TEMP_o;

  ALU alu_1 (
    .a_larger(alu_1_a_larger), .equal(alu_1_equal), .o(alu_1_o), .carry_out(alu_1_carry_out),
    .zero(alu_1_zero), .carry_in(and_1_out), .A(ACC_o), .B(TEMP_o), .operation(cu_1_op));
  NEW_REGISTER ACC (.view(out_12), .o(ACC_o), .i(alu_1_o), .set(cu_1_acc_s), .clock(clock_1_out), .enable(cu_1_acc_e));
  Clock clock_1 (.out(clock_1_out));
  and and_1 (and_1_out, cu_1_stop_ci, Flagi_c_out);
  TMP TEMP (.view(out_5), .o(TEMP_o), .i(ACC_o), .set(cu_1_temp_s), .clock(clock_1_out), .Reset(cu_1_tmp_reset));
  GENERATO_ENABLE_SET generato_enable_set_1 (
    .enable(generato_enable_set_1_enable), .set(generato_enable_set_1_set), .clk(clock_1_out));
  PSW Flagi (
    .c_out(Flagi_c_out), .al_out(Flagi_al_out), .eq_out(Flagi_eq_out), .z_out(Flagi_z_out),
    .clk(clock_1_out), .c_in(alu_1_carry_out), .al_in(alu_1_a_larger), .eq_in(alu_1_equal),
    .z_in(alu_1_zero), .set(cu_1_flags_s));
  NEW_REGISTER R0 (.view(out_1), .o(ACC_o), .i(ACC_o), .set(R0s), .clock(clock_1_out), .enable(R0e));
  NEW_REGISTER R4 (.view(out_6), .o(ACC_o), .i(ACC_o), .set(R4s), .clock(clock_1_out), .enable(R4e));
  PC pc_1 (
    .view(out_13), .PC_o(ACC_o), .PC_e(cu_1_pc_e), .PC_i(ACC_o), .PC_set(cu_1_pc_s), .PC_INC(cu_1_pc_inc),
    .RST(reset_out));
  Button reset (.out(reset_out));
  NEW_REGISTER R1 (.view(out_2), .o(ACC_o), .i(ACC_o), .set(R1s), .clock(clock_1_out), .enable(R1e));
  NEW_REGISTER R5 (.view(out_7), .o(ACC_o), .i(ACC_o), .set(R5s), .clock(clock_1_out), .enable(R5e));
  NEW_REGISTER R2 (.view(out_3), .o(ACC_o), .i(ACC_o), .set(R2s), .clock(clock_1_out), .enable(R2e));
  NEW_REGISTER R6 (.view(out_8), .o(ACC_o), .i(ACC_o), .set(R6s), .clock(clock_1_out), .enable(R6e));
  NEW_REGISTER R3 (.view(out_4), .o(ACC_o), .i(ACC_o), .set(R3s), .clock(clock_1_out), .enable(R3e));
  NEW_REGISTER R7 (.view(out_9), .o(ACC_o), .i(ACC_o), .set(R7s), .clock(clock_1_out), .enable(R7e));
  CU cu_1 (
    .op(cu_1_op), .Tmp_reset(cu_1_tmp_reset), .PC_s(cu_1_pc_s), .IR_s(cu_1_ir_s), .IAR_s(cu_1_iar_s),
    .MAR_s(cu_1_mar_s), .RAM_s(cu_1_ram_s), .ACC_s(cu_1_acc_s), .TEMP_s(cu_1_temp_s), .R0_s(R0s), .R1_s(R1s),
    .R2_s(R2s), .R3_s(R3s), .R4_s(R4s), .R5_s(R5s), .R6_s(R6s), .R7_s(R7s), .flags_s(cu_1_flags_s),
    .PC_e(cu_1_pc_e), .ROM_e(cu_1_rom_e), .RAM_e(cu_1_ram_e), .ACC_e(cu_1_acc_e), .R0_e(R0e), .R1_e(R1e),
    .R2_e(R2e), .R3_e(R3e), .R4_e(R4e), .R5_e(R5e), .R6_e(R6e), .R7_e(R7e), .Stop_ci(cu_1_stop_ci),
    .PC_INC(cu_1_pc_inc), .eq_temp(alu_1_equal), .ci(Flagi_c_out), .co(Flagi_al_out), .al(Flagi_c_out),
    .eq(Flagi_eq_out), .z(Flagi_z_out), .clk_s(generato_enable_set_1_set),
    .clk_e(generato_enable_set_1_enable), .current_instruction(ir_1_o), .clk(clock_1_out));
  IR ir_1 (.view(out_14), .o(ir_1_o), .i(ACC_o), .set(cu_1_ir_s), .clock(clock_1_out));
  RAM256 ram256_1 (
    .RAM_o(ACC_o), .out_7(out_10), .RAM_i(ACC_o), .clk(clock_1_out), .RAM_set(cu_1_ram_s),
    .RAM_enable(cu_1_ram_e), .MAR_set(cu_1_mar_s), .MAR_i(ACC_o));
  ROM256 rom256_1 (
    .out_5(out_11), .ROM_o(ACC_o), .clk(clock_1_out), .IAR_set(cu_1_iar_s), .IAR_i(ACC_o),
    .ROM_enable(cu_1_rom_e));
endmodule

module SHL (
  input  shift_in,
  input  [7:0] i,
  output [7:0] o,
  output shift_out
);


  assign o = {i[6:0], shift_in};
  assign shift_out = i[7];
endmodule

module SHR (
  input  [7:0] i,
  input  shift_in,
  output shift_out,
  output [7:0] o
);


  assign o = {shift_in, i[7:1]};
  assign shift_out = i[0];
endmodule

module ALU (
  input  [7:0] A,
  input  [7:0] B,
  input  carry_in,
  input  [2:0] operation,
  output a_larger,
  output equal,
  output zero,
  output [7:0] o,
  output carry_out
);

  wire adder_1_cout, decoder_1_out0, decoder_1_out1, decoder_1_out2, decoder_1_out3, decoder_1_out4,
       decoder_1_out5, decoder_1_out6, decoder_1_out7, shl_1_shift_out, shr_1_shift_out, subtractor_1_bout;
  wire [7:0] adder_1_out, and_1_out, not_1_out, or_1_out, shl_1_o, shr_1_o, subtractor_1_out, xor_1_out;

  assign not_1_out = ~B;  // NOT_Gate not_1, 8 bits wide
  Comparator comparator_1 (.a(A), .b(B), .gt(a_larger), .eq(equal));  // open: lt
  Subtractor subtractor_1 (.a(B), .b(A), .out(subtractor_1_out), .bin(carry_in), .bout(subtractor_1_bout));
  assign xor_1_out = A ^ B;  // XOR_Gate xor_1, 8 bits wide
  assign or_1_out = A | B;  // OR_Gate or_1, 8 bits wide
  assign and_1_out = A & B;  // AND_Gate and_1, 8 bits wide
  Adder adder_1 (.a(A), .b(B), .out(adder_1_out), .cin(carry_in), .cout(adder_1_cout));
  assign carry_out = decoder_1_out0 ? adder_1_cout : 1'bz;  // Controlled_Buffer controlled_buffer_1
  SHL shl_1 (.shift_in(carry_in), .i(A), .o(shl_1_o), .shift_out(shl_1_shift_out));
  SHR shr_1 (.i(A), .shift_in(carry_in), .shift_out(shr_1_shift_out), .o(shr_1_o));
  assign carry_out = decoder_1_out2 ? shl_1_shift_out : 1'bz;  // Controlled_Buffer controlled_buffer_2
  assign carry_out = decoder_1_out1 ? shr_1_shift_out : 1'bz;  // Controlled_Buffer controlled_buffer_3
  assign o = decoder_1_out1 ? shr_1_o : 8'bz;  // Controlled_Buffer controlled_buffer_4
  assign o = decoder_1_out0 ? adder_1_out : 8'bz;  // Controlled_Buffer controlled_buffer_5
  Decoder #(.enable("false"), .select(3)) decoder_1 (
    .out0(decoder_1_out0), .out1(decoder_1_out1), .out2(decoder_1_out2), .out3(decoder_1_out3),
    .out4(decoder_1_out4), .out5(decoder_1_out5), .out6(decoder_1_out6), .out7(decoder_1_out7),
    .sel(operation));
  assign o = decoder_1_out3 ? not_1_out : 8'bz;  // Controlled_Buffer controlled_buffer_6
  assign o = decoder_1_out2 ? shl_1_o : 8'bz;  // Controlled_Buffer controlled_buffer_7
  assign carry_out = decoder_1_out7 ? subtractor_1_bout : 1'bz;  // Controlled_Buffer controlled_buffer_8
  assign o = decoder_1_out6 ? xor_1_out : 8'bz;  // Controlled_Buffer controlled_buffer_9
  assign o = decoder_1_out5 ? or_1_out : 8'bz;  // Controlled_Buffer controlled_buffer_10
  assign o = decoder_1_out4 ? and_1_out : 8'bz;  // Controlled_Buffer controlled_buffer_11
  assign o = decoder_1_out7 ? subtractor_1_out : 8'bz;  // Controlled_Buffer controlled_buffer_12
  nor nor_1 (zero, o[0], o[1], o[2], o[3], o[4], o[5], o[6], o[7]);
endmodule

module CU (
  input  clk_s,
  input  clk,
  input  clk_e,
  input  [7:0] current_instruction,
  input  ci,
  input  co,
  input  al,
  input  eq,
  input  eq_temp,
  input  z,
  output Tmp_reset,
  output Stop_ci,
  output PC_s,
  output PC_INC,
  output IR_s,
  output flags_s,
  output IAR_s,
  output [2:0] op,
  output PC_e,
  output MAR_s,
  output ROM_e,
  output RAM_s,
  output RAM_e,
  output ACC_s,
  output ACC_e,
  output TEMP_s,
  output R0_e,
  output R0_s,
  output R1_e,
  output R1_s,
  output R2_e,
  output R2_s,
  output R3_e,
  output R3_s,
  output R4_e,
  output R4_s,
  output R5_e,
  output R5_s,
  output R6_e,
  output R6_s,
  output R7_e,
  output R7_s
);

  wire ACC_e_t, ACC_s_t, and_16_out, controlled_buffer_1_out, d_ff_1_q, d_ff_2_q, flags_s_t, IAR_s_t, IR_s_t,
       MAR_s_t, or_1_out, or_2_out, or_4_out, or_5_out, or_6_out, or_7_out, or_8_out, or_9_out, PC_e_t,
       PC_inc_t, PC_s_t, R0_e_t, R0_s_t, R1_e_t, R1_s_t, R2_e_t, R2_s_t, R3_e_t, R3_s_t, R4_e_t, R4_s_t,
       R5_e_t, R5_s_t, R6_e_t, R6_s_t, R7_e_t, R7_s_t, RAM_e_t, RAM_s_t, ROM_e_t, Step1, Step2,
       steper_1_step3, steper_1_step4, steper_1_step5, steper_1_step6, steper_1_step7, TMP_rst, TMP_s, UC_J;
  wire [1:0] and_15_out;
  wire [39:0] rom_1_data;
  wire [39:35] przejsciowka_1_o;

  and and_1 (flags_s, flags_s_t, clk_s);
  and and_2 (PC_e, or_1_out, clk_e);
  and and_3 (ROM_e, or_2_out, clk_e);
  and and_4 (RAM_e, RAM_e_t, clk_e);
  and and_5 (ACC_e, ACC_e_t, clk_e);
  and and_6 (R0_e, R0_e_t, clk_e);
  and and_7 (R1_e, R1_e_t, clk_e);
  and and_8 (R2_e, R2_e_t, clk_e);
  and and_9 (R3_e, R3_e_t, clk_e);
  and and_10 (R4_e, R4_e_t, clk_e);
  and and_11 (R5_e, R5_e_t, clk_e);
  and and_12 (R6_e, R6_e_t, clk_e);
  and and_13 (R7_e, R7_e_t, clk_e);
  or or_1 (or_1_out, PC_e_t, Step1);
  or or_2 (or_2_out, ROM_e_t, Step2);
  or or_3 (PC_INC, and_16_out, Step2);
  and and_14 (and_15_out[1], 1'b1, or_4_out);
  and and_15 (and_15_out[0], 1'b1, or_5_out);
  ROM #(.addrWidth(10), .dataWidth(40)) rom_1 (.addr({current_instruction, and_15_out}), .data(rom_1_data));
  and and_16 (and_16_out, PC_inc_t, d_ff_1_q);
  or or_4 (or_4_out, steper_1_step5, steper_1_step6);
  or or_5 (or_5_out, steper_1_step4, steper_1_step6);
  or or_6 (or_6_out, steper_1_step3, steper_1_step4, steper_1_step5, steper_1_step6);
  D_Flip_Flop d_ff_1 (.D(clk_s), .clk(clk), .Q(d_ff_1_q));  // open: Qn, preset, reset
  PRZEJSCIOWKA przejsciowka_1 (
    .o({przejsciowka_1_o, UC_J, ACC_e_t, ACC_s_t, TMP_rst, TMP_s, R0_e_t, R0_s_t, R1_e_t, R1_s_t, R2_e_t, R2_s_t, R3_e_t, R3_s_t, R4_e_t, R4_s_t, R5_e_t, R5_s_t, R6_e_t, R6_s_t, R7_e_t, R7_s_t, RAM_e_t, RAM_s_t, MAR_s_t, ROM_e_t, IAR_s_t, PC_e_t, PC_s_t, PC_inc_t, IR_s_t, op, flags_s_t, Stop_ci}),
    .i(rom_1_data), .e(or_6_out));
  STEPER steper_1 (
    .step3(steper_1_step3), .step4(steper_1_step4), .step5(steper_1_step5), .step6(steper_1_step6),
    .step7(steper_1_step7), .step1(Step1), .step2(Step2), .clk(clk), .reset(steper_1_step7));
  assign controlled_buffer_1_out = TMP_rst ? eq_temp : 1'bz;  // Controlled_Buffer controlled_buffer_1
  D_Flip_Flop d_ff_2 (.D(controlled_buffer_1_out), .clk(clk), .Q(d_ff_2_q));  // open: Qn, preset, reset
  or or_7 (or_7_out, UC_J, d_ff_2_q);
  or or_8 (or_8_out, Step2, IR_s_t);
  or or_9 (or_9_out, IAR_s_t, Step1);
  and and_17 (Tmp_reset, TMP_rst, clk_s);
  and and_18 (IR_s, or_8_out, clk_s);
  and and_19 (IAR_s, or_9_out, clk_s);
  and and_20 (MAR_s, MAR_s_t, clk_s);
  and and_21 (RAM_s, RAM_s_t, clk_s);
  and and_22 (ACC_s, ACC_s_t, clk_s);
  and and_23 (TEMP_s, TMP_s, clk_s);
  and and_24 (R0_s, R0_s_t, clk_s);
  and and_25 (R1_s, R1_s_t, clk_s);
  and and_26 (R2_s, R2_s_t, clk_s);
  and and_27 (R3_s, R3_s_t, clk_s);
  and and_28 (R4_s, R4_s_t, clk_s);
  and and_29 (R5_s, R5_s_t, clk_s);
  and and_30 (R6_s, R6_s_t, clk_s);
  and and_31 (R7_s, R7_s_t, clk_s);
  and and_32 (PC_s, or_7_out, PC_s_t, clk_s);

  // Other names for the same wires on the sheet: ENABLE = clk_e; op_0 = op[0]; op_1 = op[1]; op_2 = op[2];
  //   SET = clk_s

  // Notes on the sheet:
  //   contents of rom_1 (hex, n*v repeats v):
  //   76*0 240000000 100000007 66*0 300 240000040 100000402 0 300 c40 240000000 100002002 8*0 240000000
  //   120000002 0 0 240000000 108000002 38*0 240000000 10000000b 0 0 300 240000040 100000403 13*0
  //   240000000 120000003 0 0 240000000 108000003 58*0 240000000 120000014 62*0 240000000 120000010 30*0
  //   280000000 300 4c0 29*0 240000000 120000018 46*0 300 100000440 14*0 300 10000440 0 0 300 4000440
  //   106*0 300 240000040 10000041f 0 300 c40 240000000 10000201f 8*0 240000000 12000001f 0 0 240000000
  //   10800001f 58*0 300 c40 10002000 0 300 c40 4002000 221*0 300 4000004c0 10*0 80000000 100000000 0 0
  //   300 c40 100002000 0 20000800 100002000 0 0 8000800 100002000 0 0 120000000 0 0 0 108000000 0 0 0
  //   102000000 0 0 0 100800000 0 0 0 100200000 0 0 0 100080000 0 0 0 100020000 0 0 0 100008000 19*0
  //   240000000 10000000c 0 0 300 c00 200001000 9*0 210000000 0 0 0 204000000
endmodule

module NEW_REGISTER (
  input  [7:0] i,
  input  enable,
  input  set,
  input  clock,
  output [7:0] view,
  output [7:0] o
);

  Register register_1 (.D(i), .en(set), .Q(view), .clk(clock));  // open: clr
  assign o = enable ? view : 8'bz;  // Controlled_Buffer controlled_buffer_1
endmodule

module ROM256 (
  input  [7:0] IAR_i,
  input  clk,
  input  IAR_set,
  input  ROM_enable,
  output [7:0] out_5,
  output [7:0] ROM_o
);

  wire [7:0] IAR_o, rom_1_data;

  ROM rom_1 (.addr(IAR_o), .data(rom_1_data));
  NEW_REGISTER IAR (.view(out_5), .o(IAR_o), .i(IAR_i), .set(IAR_set), .clock(clk), .enable(1'b1));
  assign ROM_o = ROM_enable ? rom_1_data : 8'bz;  // Controlled_Buffer controlled_buffer_1
endmodule

module RAM256 (
  input  [7:0] MAR_i,
  input  MAR_set,
  input  clk,
  input  RAM_set,
  input  RAM_enable,
  input  [7:0] RAM_i,
  output [7:0] out_7,
  output [7:0] RAM_o
);

  wire [7:0] MAR_o, ram_1_dout;

  RAM ram_1 (.addr(MAR_o), .we(RAM_set), .oe(RAM_enable), .clk(clk), .din(RAM_i), .dout(ram_1_dout));
  NEW_REGISTER MAR (.view(out_7), .o(MAR_o), .i(MAR_i), .set(MAR_set), .clock(clk), .enable(1'b1));
  assign RAM_o = RAM_enable ? ram_1_dout : 8'bz;  // Controlled_Buffer controlled_buffer_1
endmodule

module TMP (
  input  [7:0] i,
  input  set,
  input  clock,
  input  Reset,
  output [7:0] view,
  output [7:0] o
);

  Register register_1 (.D(i), .en(set), .Q(o), .clk(clock), .clr(Reset));

  assign view = o;
endmodule

module PC (
  input  PC_set,
  input  [7:0] PC_i,
  input  RST,
  input  PC_INC,
  input  PC_e,
  output [7:0] view,
  output [7:0] PC_o
);

  Counter counter_1 (.load(PC_set), .D(PC_i), .Q(view), .clk(PC_INC), .clr(RST));  // open: count, carry, up
  assign PC_o = PC_e ? view : 8'bz;  // Controlled_Buffer controlled_buffer_1
endmodule

module GENERATO_ENABLE_SET (
  input  clk,
  output set,
  output enable
);

  wire d_ff_1_q, d_ff_3_q, d_ff_4_q, d_ff_5_q;

  D_Flip_Flop #(.trigger("falling")) d_ff_1 (.D(1'b1), .clk(clk), .Q(d_ff_1_q), .reset(d_ff_5_q));  // open: Qn, preset
  D_Flip_Flop d_ff_2 (.D(d_ff_1_q), .clk(clk), .Q(enable), .reset(d_ff_5_q));  // open: Qn, preset
  D_Flip_Flop d_ff_3 (.D(enable), .clk(clk), .Q(d_ff_3_q), .reset(d_ff_5_q));  // open: Qn, preset
  xor xor_1 (set, d_ff_3_q, d_ff_4_q);
  D_Flip_Flop d_ff_4 (.D(d_ff_3_q), .clk(clk), .Q(d_ff_4_q), .reset(d_ff_5_q));  // open: Qn, preset
  D_Flip_Flop d_ff_5 (.D(d_ff_4_q), .clk(clk), .Q(d_ff_5_q), .reset(d_ff_5_q));  // open: Qn, preset
endmodule

module IR (
  input  [7:0] i,
  input  set,
  input  clock,
  output [7:0] view,
  output [7:0] o
);

  Register register_1 (.D(i), .en(set), .Q(o), .clk(clock));  // open: clr

  assign view = o;
endmodule

module BANK_REGISTERS (
  input  [7:0] in_1,
  input  clk,
  input  e_set,
  input  [2:0] set,
  input  [2:0] enable,
  input  e_enable,
  output [7:0] out_7,
  output [7:0] out_8,
  output [7:0] out_9,
  output [7:0] out_10,
  output [7:0] out_11,
  output [7:0] out_12,
  output [7:0] out_13,
  output [7:0] out_14,
  output [7:0] out_15
);

  wire decoder_1_out0, decoder_1_out1, decoder_1_out2, decoder_1_out3, decoder_1_out4, decoder_1_out5,
       decoder_1_out6, decoder_1_out7, decoder_2_out0, decoder_2_out1, decoder_2_out2, decoder_2_out3,
       decoder_2_out4, decoder_2_out5, decoder_2_out6, decoder_2_out7;
  wire [7:0] demultiplexer_1_out0, demultiplexer_1_out1, demultiplexer_1_out2, demultiplexer_1_out3,
       demultiplexer_1_out4, demultiplexer_1_out5, demultiplexer_1_out6, demultiplexer_1_out7, REG0_o,
       REG1_o, REG2_o, REG3_o, REG4_o, REG5_o, REG6_o, REG7_o;

  Decoder #(.select(3)) decoder_1 (
    .out0(decoder_1_out0), .out1(decoder_1_out1), .out2(decoder_1_out2), .out3(decoder_1_out3),
    .out4(decoder_1_out4), .out5(decoder_1_out5), .out6(decoder_1_out6), .out7(decoder_1_out7), .sel(set),
    .en(e_set));
  Demultiplexer #(.select(3), .width(8)) demultiplexer_1 (
    .out0(demultiplexer_1_out0), .out1(demultiplexer_1_out1), .out2(demultiplexer_1_out2),
    .out3(demultiplexer_1_out3), .out4(demultiplexer_1_out4), .out5(demultiplexer_1_out5),
    .out6(demultiplexer_1_out6), .out7(demultiplexer_1_out7), .in(in_1), .sel(set));
  NEW_REGISTER REG0 (
    .view(out_8), .o(REG0_o), .i(demultiplexer_1_out0), .set(decoder_1_out0), .clock(clk),
    .enable(decoder_2_out0));
  NEW_REGISTER REG1 (
    .view(out_9), .o(REG1_o), .i(demultiplexer_1_out1), .set(decoder_1_out1), .clock(clk),
    .enable(decoder_2_out1));
  NEW_REGISTER REG2 (
    .view(out_10), .o(REG2_o), .i(demultiplexer_1_out2), .set(decoder_1_out2), .clock(clk),
    .enable(decoder_2_out2));
  NEW_REGISTER REG3 (
    .view(out_11), .o(REG3_o), .i(demultiplexer_1_out3), .set(decoder_1_out3), .clock(clk),
    .enable(decoder_2_out3));
  NEW_REGISTER REG4 (
    .view(out_12), .o(REG4_o), .i(demultiplexer_1_out4), .set(decoder_1_out4), .clock(clk),
    .enable(decoder_2_out4));
  NEW_REGISTER REG5 (
    .view(out_13), .o(REG5_o), .i(demultiplexer_1_out5), .set(decoder_1_out5), .clock(clk),
    .enable(decoder_2_out5));
  NEW_REGISTER REG6 (
    .view(out_14), .o(REG6_o), .i(demultiplexer_1_out6), .set(decoder_1_out6), .clock(clk),
    .enable(decoder_2_out6));
  Multiplexer #(.select(3), .width(8)) multiplexer_1 (
    .in0(REG0_o), .in1(REG1_o), .in2(REG2_o), .in3(REG3_o), .in4(REG4_o), .in5(REG5_o), .in6(REG6_o),
    .in7(REG7_o), .out(out_7), .sel(enable));
  Decoder #(.select(3)) decoder_2 (
    .out0(decoder_2_out0), .out1(decoder_2_out1), .out2(decoder_2_out2), .out3(decoder_2_out3),
    .out4(decoder_2_out4), .out5(decoder_2_out5), .out6(decoder_2_out6), .out7(decoder_2_out7), .sel(enable),
    .en(e_enable));
  NEW_REGISTER REG7 (
    .view(out_15), .o(REG7_o), .i(demultiplexer_1_out7), .set(decoder_1_out7), .clock(clk),
    .enable(decoder_2_out7));
endmodule

module PSW (
  input  c_in,
  input  al_in,
  input  eq_in,
  input  z_in,
  input  clk,
  input  set,
  output c_out,
  output al_out,
  output eq_out,
  output z_out
);

  wire controlled_buffer_1_out, controlled_buffer_2_out, controlled_buffer_3_out, controlled_buffer_4_out;

  assign controlled_buffer_1_out = set ? c_in : 1'bz;  // Controlled_Buffer controlled_buffer_1
  assign controlled_buffer_2_out = set ? al_in : 1'bz;  // Controlled_Buffer controlled_buffer_2
  assign controlled_buffer_3_out = set ? eq_in : 1'bz;  // Controlled_Buffer controlled_buffer_3
  assign controlled_buffer_4_out = set ? z_in : 1'bz;  // Controlled_Buffer controlled_buffer_4
  D_Flip_Flop d_ff_1 (.D(controlled_buffer_1_out), .clk(clk), .Q(c_out));  // open: Qn, preset, reset
  D_Flip_Flop d_ff_2 (.D(controlled_buffer_2_out), .clk(clk), .Q(al_out));  // open: Qn, preset, reset
  D_Flip_Flop d_ff_3 (.D(controlled_buffer_3_out), .clk(clk), .Q(eq_out));  // open: Qn, preset, reset
  D_Flip_Flop d_ff_4 (.D(controlled_buffer_4_out), .clk(clk), .Q(z_out));  // open: Qn, preset, reset
endmodule

module STEPER (
  input  clk,
  input  reset,
  output step5,
  output step6,
  output step2,
  output step3,
  output step4,
  output step7,
  output step1
);

  wire d_ff_1_q, d_ff_2_q, d_ff_3_q, d_ff_4_q, d_ff_5_q, d_ff_6_q, d_ff_7_q, d_ff_8_q, d_ff_9_q, d_ff_10_q,
       d_ff_11_q, d_ff_12_q, d_ff_13_q, d_ff_14_q, d_ff_15_q, d_ff_16_q, d_ff_17_q, d_ff_18_q, d_ff_19_q,
       d_ff_20_q, d_ff_21_q, d_ff_22_q, d_ff_23_q, d_ff_24_q, not_2_out, not_3_out, not_4_out, not_5_out,
       not_6_out;

  D_Flip_Flop #(.trigger("falling")) d_ff_1 (.D(1'b1), .clk(clk), .Q(d_ff_1_q), .reset(reset));  // open: Qn, preset
  D_Flip_Flop d_ff_2 (.D(d_ff_1_q), .clk(clk), .Q(d_ff_2_q), .reset(reset));  // open: Qn, preset
  D_Flip_Flop d_ff_3 (.D(d_ff_2_q), .clk(clk), .Q(d_ff_3_q), .reset(reset));  // open: Qn, preset
  not not_1 (step1, d_ff_5_q);
  D_Flip_Flop d_ff_4 (.D(d_ff_3_q), .clk(clk), .Q(d_ff_4_q), .reset(reset));  // open: Qn, preset
  D_Flip_Flop d_ff_5 (.D(d_ff_4_q), .clk(clk), .Q(d_ff_5_q), .reset(reset));  // open: Qn, preset
  and and_1 (step2, d_ff_5_q, not_2_out);
  D_Flip_Flop d_ff_6 (.D(d_ff_5_q), .clk(clk), .Q(d_ff_6_q), .reset(reset));  // open: Qn, preset
  D_Flip_Flop d_ff_7 (.D(d_ff_6_q), .clk(clk), .Q(d_ff_7_q), .reset(reset));  // open: Qn, preset
  not not_2 (not_2_out, d_ff_9_q);
  D_Flip_Flop d_ff_8 (.D(d_ff_7_q), .clk(clk), .Q(d_ff_8_q), .reset(reset));  // open: Qn, preset
  D_Flip_Flop d_ff_9 (.D(d_ff_8_q), .clk(clk), .Q(d_ff_9_q), .reset(reset));  // open: Qn, preset
  and and_2 (step3, d_ff_9_q, not_3_out);
  D_Flip_Flop d_ff_10 (.D(d_ff_9_q), .clk(clk), .Q(d_ff_10_q), .reset(reset));  // open: Qn, preset
  not not_3 (not_3_out, d_ff_13_q);
  D_Flip_Flop d_ff_11 (.D(d_ff_10_q), .clk(clk), .Q(d_ff_11_q), .reset(reset));  // open: Qn, preset
  D_Flip_Flop d_ff_12 (.D(d_ff_11_q), .clk(clk), .Q(d_ff_12_q), .reset(reset));  // open: Qn, preset
  D_Flip_Flop d_ff_13 (.D(d_ff_12_q), .clk(clk), .Q(d_ff_13_q), .reset(reset));  // open: Qn, preset
  and and_3 (step4, d_ff_13_q, not_4_out);
  D_Flip_Flop d_ff_14 (.D(d_ff_13_q), .clk(clk), .Q(d_ff_14_q), .reset(reset));  // open: Qn, preset
  D_Flip_Flop d_ff_15 (.D(d_ff_14_q), .clk(clk), .Q(d_ff_15_q), .reset(reset));  // open: Qn, preset
  not not_4 (not_4_out, d_ff_17_q);
  D_Flip_Flop d_ff_16 (.D(d_ff_15_q), .clk(clk), .Q(d_ff_16_q), .reset(reset));  // open: Qn, preset
  D_Flip_Flop d_ff_17 (.D(d_ff_16_q), .clk(clk), .Q(d_ff_17_q), .reset(reset));  // open: Qn, preset
  and and_4 (step5, d_ff_17_q, not_5_out);
  D_Flip_Flop d_ff_18 (.D(d_ff_17_q), .clk(clk), .Q(d_ff_18_q), .reset(reset));  // open: Qn, preset
  D_Flip_Flop d_ff_19 (.D(d_ff_18_q), .clk(clk), .Q(d_ff_19_q), .reset(reset));  // open: Qn, preset
  not not_5 (not_5_out, d_ff_21_q);
  D_Flip_Flop d_ff_20 (.D(d_ff_19_q), .clk(clk), .Q(d_ff_20_q), .reset(reset));  // open: Qn, preset
  D_Flip_Flop d_ff_21 (.D(d_ff_20_q), .clk(clk), .Q(d_ff_21_q), .reset(reset));  // open: Qn, preset
  and and_5 (step6, d_ff_21_q, not_6_out);
  D_Flip_Flop d_ff_22 (.D(d_ff_21_q), .clk(clk), .Q(d_ff_22_q), .reset(reset));  // open: Qn, preset
  D_Flip_Flop d_ff_23 (.D(d_ff_22_q), .clk(clk), .Q(d_ff_23_q), .reset(reset));  // open: Qn, preset
  not not_6 (not_6_out, step7);
  D_Flip_Flop d_ff_24 (.D(d_ff_23_q), .clk(clk), .Q(d_ff_24_q), .reset(reset));  // open: Qn, preset
  D_Flip_Flop d_ff_25 (.D(d_ff_24_q), .clk(clk), .Q(step7), .reset(reset));  // open: Qn, preset
endmodule

module PRZEJSCIOWKA (
  input  e,
  input  [39:0] i,
  output [39:0] o
);

  and and_1 (o[0], i[0], e);
  and and_2 (o[1], i[1], e);
  and and_3 (o[2], i[2], e);
  and and_4 (o[3], i[3], e);
  and and_5 (o[4], i[4], e);
  and and_6 (o[5], i[5], e);
  and and_7 (o[6], i[6], e);
  and and_8 (o[7], i[7], e);
  and and_9 (o[8], i[8], e);
  and and_10 (o[9], i[9], e);
  and and_11 (o[10], i[10], e);
  and and_12 (o[11], i[11], e);
  and and_13 (o[12], i[12], e);
  and and_14 (o[13], i[13], e);
  and and_15 (o[14], i[14], e);
  and and_16 (o[15], i[15], e);
  and and_17 (o[16], i[16], e);
  and and_18 (o[17], i[17], e);
  and and_19 (o[18], i[18], e);
  and and_20 (o[19], i[19], e);
  and and_21 (o[20], i[20], e);
  and and_22 (o[21], i[21], e);
  and and_23 (o[22], i[22], e);
  and and_24 (o[23], i[23], e);
  and and_25 (o[24], i[24], e);
  and and_26 (o[25], i[25], e);
  and and_27 (o[26], i[26], e);
  and and_28 (o[27], i[27], e);
  and and_29 (o[28], i[28], e);
  and and_30 (o[29], i[29], e);
  and and_31 (o[30], i[30], e);
  and and_32 (o[31], i[31], e);
  and and_33 (o[32], i[32], e);
  and and_34 (o[33], i[33], e);
  and and_35 (o[34], i[34], e);
  and and_36 (o[35], i[35], e);
  and and_37 (o[36], i[36], e);
  and and_38 (o[37], i[37], e);
  and and_39 (o[38], i[38], e);
  and and_40 (o[39], i[39], e);
endmodule
